# Fritzing sketch circuit_diagram (saved by Fritzing 0.8.5b)
breadboards: 1

parts:
  R1 = Resistor [tolerance=±5% resistance=270 package=THT]
  Raspberry_Pi_B_rev1 = Raspberry Pi B rev1
  LED1 = LED - 5mm [color="Red (633nm)" package="5 mm [THT]"]
  LED2 = LED - 5mm [color="Green (555nm)" package="5 mm [THT]"]
  S1 = Momentary Switch [package=ksa_sealed_tac_switch]
  R2 = Resistor [tolerance=±5% resistance=270 package=THT]
  IR1 = TSOP312.., 314.. [package=THT]
  IR2 = TSOP312.., 314.. [package=THT]
  LED3 = LED - 5mm [color="Infrared (850nm)" package="5 mm [THT]"]
  LED4 = LED - 5mm [color="Infrared (850nm)" package="5 mm [THT]"]

nets:
  GND: R1.Pin_0, Raspberry_Pi_B_rev1.GND, S1.3, S1.4, R2.Pin_0, IR1.GND, IR2.GND, LED3.cathode, LED4.cathode
  N1: R1.Pin_1, LED2.cathode
  N2: Raspberry_Pi_B_rev1.3V3, IR1.Vs, IR2.Vs
  N3: Raspberry_Pi_B_rev1.5V, LED3.anode, LED4.anode
  N4: Raspberry_Pi_B_rev1.GPIO_14, LED2.anode
  N5: Raspberry_Pi_B_rev1.GPIO_15, IR1.Data
  N6: Raspberry_Pi_B_rev1.GPIO_18, LED1.anode
  N7: Raspberry_Pi_B_rev1.GPIO_4, IR2.Data
  N8: Raspberry_Pi_B_rev1.GPIO_7, S1.1, S1.2
  N9: LED1.cathode, R2.Pin_1
